# Fritzing sketch arduino_range_meter_and_display (saved by Fritzing 0.8.7b)
circuit board: 6.88566cm x 5.36311cm
breadboards: 1

parts:
  Part1 = Arduino Uno (Rev3)
  SONAR1 = Maxbotix MaxSonar Ultrasonic Sensor

nets:
  GND: Part1.GND, SONAR1.GND
  N1: Part1.D3_PWM, SONAR1.PW
  5V: Part1.5V, SONAR1.+5V

custom parts:
  Maxbotix MaxSonar Ultrasonic Sensor: Maxbotix MaxSonar Ultrasonic Sensor LV-EZ0, LV-EZ1, LV-EZ2, LV-EZ3, LV-EZ4
